# Fritzing sketch raspi3_proximity-sensor (saved by Fritzing 0.9.5d)

parts:
  VCNL1 = proximity sensor
  Raspberry_Pi_1 = Raspberry Pi 3 [part_number=RPI-3-V1.2]

nets:
  VIN: VCNL1.VIN, Raspberry_Pi_1.3v3
  GND: VCNL1.GND, Raspberry_Pi_1.GND
  N1: VCNL1.SCL, Raspberry_Pi_1.GPIO3
  N2: VCNL1.SDA, Raspberry_Pi_1.GPIO2

custom parts:
  proximity sensor: This is a VCNL4010 Proximity and Ambient Light Sensor module sold by Switch Science (Japan). It integrates an infrared emitter and photodiodes for proximity sensing, along with an ambient light sensor. The module communicates via I2C and operates at 3.3V or 5V. Based on the design from SparkFun, this board allows easy integration with microcontrollers for gesture recognition, object detection,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
